# Fritzing sketch hall effect (saved by Fritzing 0.9.2b)
breadboards: 1

parts:
  Part1 = Arduino Uno (Rev3)
  U1 = TEMPERATURE-SENSOR [package=to-92]
  R1 = Resistor [tolerance=±5% resistance=220 package=THT]

nets:
  N1: Part1.GND, U1.ADJ
  N2: Part1.D6_PWM, U1.GND, R1.Pin_1
  5V: Part1.5V, U1.VCC, R1.Pin_0
